# Fritzing sketch boiler_pubsub_wemos (saved by Fritzing 0.9.3b)

parts:
  U1 = 2-Channel 5v Relay Shield [package=relay-2ch5v10a]
  U2 = 2-Channel 5v Relay Shield [package=relay-2ch5v10a]
  DS1 = DS18B20 1-Wire Temperature Sensor [part_number=DS18B20]
  DS2 = DS18B20 1-Wire Temperature Sensor [part_number=DS18B20]
  LED1 = LED - 5mm [color="Red (633nm)" package="5 mm [THT]"]
  LED2 = LED - 5mm [color="Green (560nm)" package="5 mm [THT]"]
  S1 = Pushbutton [package="[THT]"]
  S2 = Pushbutton [package="[THT]"]
  AMS1 = AMS1777 5V regulator module
  M1 = WeMos D1 Mini V4.0.0
  R2 = Resistor [tolerance=±5% resistance=220 package=THT]
  R3 = Resistor [tolerance=±5% resistance=220 package=THT]
  R4 = Resistor [tolerance=±5% resistance=10k package=THT]
  R5 = Resistor [tolerance=±5% resistance=10k package=THT]

nets:
  VDD: U1.VCC, DS1.VDD, DS2.VDD, AMS1.VIN+, R5.Pin_0
  N1: U1.IN1, M1.A0
  N2: U1.IN2, M1.16
  N3: U1.K1-On, U1.K2-In, U1.K2-Off, U1.K2-On, U1.JD-GND
  GND: U2.GND, DS1.GND, DS2.GND, LED1.cathode, LED2.cathode, S1.Pin_1, S1.Pin_2, S2.Pin_1, S2.Pin_2, AMS1.GND-_(input)
  N4: U2.IN1, M1.TX
  N5: U2.IN2, M1.RX
  N6: U2.K1-On, U2.K2-In, U2.K2-Off
  N7: DS1.DQ, DS2.DQ, M1.2/LED
  N8: LED1.anode, R2.Pin_1
  N9: LED2.anode, R3.Pin_1
  N10: S1.Pin_3, S1.Pin_4, M1.14/SCK, R4.Pin_1
  N11: S2.Pin_3, S2.Pin_4, M1.12/MISO, R5.Pin_1
  N12: AMS1.VOUT+, M1.3.3V
  N13: M1.13/MOSI, R3.Pin_0
  N14: M1.15, R2.Pin_0

notes:
  Насос ТТК
  Бойлер
  Блокировка ГК
  Вкл ГК

custom parts:
  2-Channel 5v Relay Shield: 2 Channel 5v Relay Shield w. 2x SPD-06VDC-SD-C
  AMS1777 5V regulator module: AMS1777 5V regulator module source : https://github.com/ShenTengTu/fritzing_parts/tree/master/voltage%20regulator/AMS1117_5V_regulator_module
  WeMos D1 Mini V4.0.0: The D1 mini is a mini wifi board based on ESP-8266EX.
