# Fritzing sketch mqtt_w5500 (saved by Fritzing 0.9.3b)

parts:
  U1 = 2-Channel 5v Relay Shield [package=relay-2ch5v10a]
  U2 = 2-Channel 5v Relay Shield [package=relay-2ch5v10a]
  W5500_Module1 = W5500 Ethernet module [package="DIP (Dual Inline) [THT]"]
  DS1 = DS18B20 1-Wire Temperature Sensor [part_number=DS18B20]
  DS2 = DS18B20 1-Wire Temperature Sensor [part_number=DS18B20]
  R1 = Resistor [tolerance=±5% resistance=10k package=THT]
  LED1 = LED - 5mm [color="Red (633nm)" package="5 mm [THT]"]
  LED2 = LED - 5mm [color="Green (560nm)" package="5 mm [THT]"]
  R2 = Resistor [tolerance=±5% resistance=220 package=THT]
  R3 = Resistor [tolerance=±5% resistance=220 package=THT]
  S1 = Pushbutton [package="[THT]"]
  S2 = Pushbutton [package="[THT]"]
  Часть1 = Arduino Nano (Rev3.0)

nets (from the breadboard view):
  VCC: U1.VCC, U2.VCC, Часть1.5V
  GND: U1.GND, U2.GND, Часть1.GND
  N1: U1.IN1, Часть1.D5
  N2: U1.IN2, Часть1.D6
  N3: U2.IN1, Часть1.D3
  N4: U2.IN2, Часть1.D4
  N5: W5500_Module1.MISO, Часть1.D12/MISO
  N6: W5500_Module1.MOSI, Часть1.D11/MOSI
  N7: W5500_Module1.SCS, Часть1.D10
  N8: W5500_Module1.SCLK, Часть1.D13/SCK
  N9: W5500_Module1.RST, Часть1.RESET
  GND_2: DS1.GND, DS2.GND, R1.Pin_0
  N10: DS1.DQ, DS2.DQ, Часть1.D8
  VDD: DS1.VDD, DS2.VDD
  N11: LED1.anode, R2.Pin_0
  N12: LED2.anode, R3.Pin_0
  N13: S1.Pin_1, S1.Pin_2
  N14: S1.Pin_3, S1.Pin_4, Часть1.A0
  N15: S2.Pin_3, S2.Pin_4, Часть1.D7

notes:
  Насос ТТК
  Бойлер
  Блокировка ГК
  Вкл ГК
  LCD
  SDA -> A4
  SCL -> A5

custom parts:
  2-Channel 5v Relay Shield: 2 Channel 5v Relay Shield w. 2x SPD-06VDC-SD-C
  W5500 Ethernet module: W5500 based SPI Ethernet module for Arduino, etc.
